# Fritzing sketch led_bread (saved by Fritzing 0.9.3b)
breadboards: 1

parts:
  obniz1 = obniz
  LED1 = smd LED [color="Blue (430nm)" package="0805 [SMD]"]
  R1 = Resistor [tolerance=±5% resistance=220 package=THT]

nets:
  N1: obniz1.io1, LED1.cathode, R1.Pin_0
  N2: LED1.anode, R1.Pin_1

custom parts:
  obniz: obniz is a microcontroller board based
